// Logisim project emdebbedproject.circ as structural Verilog
module main (
  input  [4:0] in_1,
  input  in_2,
  input  [3:0] in_3,
  input  in_4,
  input  in_5,
  input  in_6,
  input  in_7
);

  wire and_1_out, and_2_out, and_3_out, and_4_out, and_5_out, and_6_out, and_7_out, and_8_out, clock_1_out,
       decoder_1_out1, decoder_1_out2, decoder_2_out0, decoder_2_out1, decoder_2_out2, decoder_2_out3,
       decoder_3_out0, decoder_3_out1, decoder_3_out2, decoder_3_out3;
  wire [1:0] program_unit_1_addr0, program_unit_1_addr2, program_unit_1_mode0, program_unit_1_reg1;
  wire [2:0] program_unit_1_op0;
  wire [7:0] alu_1_result, multiplexer_1_out, multiplexer_2_out, ram_1_data, register_1_q, register_2_q,
       register_3_q, register_4_q;

  Clock clock_1 (.out(clock_1_out));
  Multiplexer #(.select(2), .width(8), .enable("false")) multiplexer_1 (
    .in0(register_1_q), .in1(register_2_q), .in2(register_3_q), .in3(register_4_q), .out(multiplexer_1_out),
    .sel(program_unit_1_addr2));
  Multiplexer #(.select(2), .width(8), .enable("false")) multiplexer_2 (
    .in0(register_1_q), .in1(register_2_q), .in2(register_3_q), .in3(register_4_q), .out(multiplexer_2_out),
    .sel(program_unit_1_addr0));
  Alu alu_1 (
    .Regis0(multiplexer_1_out), .Regis1(multiplexer_2_out), .Opcode(program_unit_1_op0),
    .Result(alu_1_result), .Status(in_1));
  Register register_1 (.D(ram_1_data), .en(and_1_out), .Q(register_1_q), .clk(clock_1_out), .clr(and_5_out));
  and and_1 (and_1_out, decoder_1_out1, decoder_2_out0);
  and and_2 (and_2_out, decoder_1_out1, decoder_2_out1);
  Decoder #(.select(2), .enable("false")) decoder_1 (
    .out1(decoder_1_out1), .out2(decoder_1_out2), .sel(program_unit_1_mode0));  // open: out0, out3
  Register register_2 (.D(ram_1_data), .en(and_2_out), .Q(register_2_q), .clk(clock_1_out), .clr(and_6_out));
  and and_3 (and_3_out, decoder_1_out1, decoder_2_out3);
  and and_4 (and_4_out, decoder_1_out1, decoder_2_out2);
  Decoder #(.select(2), .enable("false")) decoder_2 (
    .out0(decoder_2_out0), .out1(decoder_2_out1), .out2(decoder_2_out2), .out3(decoder_2_out3),
    .sel(program_unit_1_reg1));
  Program_unit program_unit_1 (
    .SINPUT(in_2), .RSTR(in_4), .EBLM(in_5), .in_1(in_3), .EBLR1(in_6), .EBLR0(in_7), .Reloj(clock_1_out),
    .OP2(program_unit_1_op0[2]), .OP1(program_unit_1_op0[1]), .OP0(program_unit_1_op0[0]),
    .Mode1(program_unit_1_mode0[1]), .Mode0(program_unit_1_mode0[0]), .ADDR3(program_unit_1_addr2[1]),
    .ADDR2(program_unit_1_addr2[0]), .ADDR1(program_unit_1_addr0[1]), .ADDR0(program_unit_1_addr0[0]),
    .REG1(program_unit_1_reg1[0]), .REG0(program_unit_1_reg1[1]));
  Register register_3 (.D(ram_1_data), .en(and_4_out), .Q(register_3_q), .clk(clock_1_out), .clr(and_7_out));
  and and_5 (and_5_out, decoder_1_out2, decoder_3_out0);
  Register register_4 (.D(ram_1_data), .en(and_3_out), .Q(register_4_q), .clk(clock_1_out), .clr(and_8_out));
  and and_6 (and_6_out, decoder_1_out2, decoder_3_out1);
  and and_7 (and_7_out, decoder_1_out2, decoder_3_out2);
  Decoder #(.select(2), .enable("false")) decoder_3 (
    .out0(decoder_3_out0), .out1(decoder_3_out1), .out2(decoder_3_out2), .out3(decoder_3_out3),
    .sel(program_unit_1_reg1));
  and and_8 (and_8_out, decoder_1_out2, decoder_3_out3);
  RAM #(.addrWidth(4), .bus("separate")) ram_1 (
    .addr({program_unit_1_addr2, program_unit_1_addr0}), .din(alu_1_result), .data(ram_1_data),
    .str(decoder_1_out1), .clk(clock_1_out), .ld(decoder_1_out2));  // open: sel, clr
endmodule

module Program_unit (
  input  [3:0] in_1,
  input  EBLR0,
  input  SINPUT,
  input  RSTR,
  input  EBLM,
  input  EBLR1,
  input  Reloj,
  output OP2,
  output OP1,
  output OP0,
  output REG1,
  output REG0,
  output Mode1,
  output Mode0,
  output ADDR3,
  output ADDR2,
  output ADDR1,
  output ADDR0
);

  wire d_ff_1_q, d_ff_2_q, d_ff_3_q, d_ff_4_q;
  wire [3:0] counter_1_q, multiplexer_1_out, rom_1_data;

  Multiplexer #(.width(4), .enable("false")) multiplexer_1 (
    .in0(in_1), .in1(counter_1_q), .out(multiplexer_1_out), .sel(SINPUT));
  Counter #(.width(4), .max('hf)) counter_1 (
    .load(EBLR0), .D(multiplexer_1_out), .Q(counter_1_q), .clk(Reloj), .clr(RSTR));  // open: count, carry
  ROM #(.addrWidth(4), .dataWidth(4)) rom_1 (.addr(multiplexer_1_out), .data(rom_1_data), .sel(EBLM));
  D_Flip_Flop d_ff_1 (.clk(Reloj), .D(rom_1_data[0]), .Q(d_ff_1_q), .en(EBLR1));  // open: Qn, preset, reset
  D_Flip_Flop d_ff_2 (.clk(Reloj), .D(rom_1_data[1]), .Q(d_ff_2_q), .en(EBLR1));  // open: Qn, preset, reset
  D_Flip_Flop d_ff_3 (.clk(Reloj), .D(rom_1_data[2]), .Q(d_ff_3_q), .en(EBLR1));  // open: Qn, preset, reset
  D_Flip_Flop d_ff_4 (.clk(Reloj), .D(rom_1_data[3]), .Q(d_ff_4_q), .en(EBLR1));  // open: Qn, preset, reset
  ContCirc8bit contcirc8bit_1 (
    .C3(d_ff_1_q), .C2(d_ff_2_q), .OP2(OP2), .C1(d_ff_3_q), .C0(d_ff_4_q), .OP1(OP1), .OP0(OP0), .RG1(REG1),
    .RG0(REG0), .MO1(Mode1), .MO0(Mode0), .ADDR3(ADDR3), .ADDR2(ADDR2), .ADDR1(ADDR1), .ADDR0(ADDR0));

  // Notes on the sheet:
  //   contents of rom_1 (hex, n*v repeats v):
  //   1 2 3 4 7 2 1 5 6 6 7 8 a f c e
  //   Opcode xx
  //   00 Store
  //   01 Read
  //   10 Add
  //   11 Rest
  //   Destination xx
endmodule

// Regis1
module Alu (
  input  [7:0] Regis0,
  input  [7:0] Regis1,
  input  [4:0] Status,
  input  [2:0] Opcode,
  output [7:0] Result
);

  wire [7:0] adder_1_out, demultiplexer_1_out0, demultiplexer_1_out1, demultiplexer_1_out2,
       demultiplexer_1_out3, demultiplexer_1_out4, demultiplexer_1_out5, demultiplexer_2_out0,
       demultiplexer_2_out1, demultiplexer_2_out2, demultiplexer_2_out3, demultiplexer_2_out5, divider_1_out,
       multiplier_1_out, negator_1_out, subtractor_1_out;

  Demultiplexer #(.select(3), .width(8), .enable("false")) demultiplexer_1 (
    .out0(demultiplexer_1_out0), .out1(demultiplexer_1_out1), .out2(demultiplexer_1_out2),
    .out3(demultiplexer_1_out3), .out4(demultiplexer_1_out4), .out5(demultiplexer_1_out5), .in(Regis0),
    .sel(Opcode));  // open: out6, out7
  Demultiplexer #(.select(3), .width(8), .enable("false")) demultiplexer_2 (
    .out0(demultiplexer_2_out0), .out1(demultiplexer_2_out1), .out2(demultiplexer_2_out2),
    .out3(demultiplexer_2_out3), .out5(demultiplexer_2_out5), .in(Regis1), .sel(Opcode));  // open: out4, out6, out7
  Adder adder_1 (.a(demultiplexer_1_out0), .b(demultiplexer_2_out0), .out(adder_1_out), .cout(Status[0]));  // open: cin
  Subtractor subtractor_1 (
    .a(demultiplexer_1_out1), .b(demultiplexer_2_out1), .out(subtractor_1_out), .bin(Status[1]));  // open: bout
  Multiplier multiplier_1 (
    .a(demultiplexer_1_out2), .b(demultiplexer_2_out2), .out(multiplier_1_out));  // open: cin, cout
  Divider divider_1 (.a(demultiplexer_1_out3), .b(demultiplexer_2_out3), .out(divider_1_out));  // open: upper, rem
  Negator negator_1 (.in(demultiplexer_1_out4), .out(negator_1_out));
  Comparator comparator_1 (
    .a(demultiplexer_1_out5), .b(demultiplexer_2_out5), .gt(Status[2]), .eq(Status[3]), .lt(Status[4]));
  Multiplexer #(.select(3), .width(8), .enable("false")) multiplexer_1 (
    .in0(adder_1_out), .in1(subtractor_1_out), .in2(multiplier_1_out), .in3(divider_1_out),
    .in4(negator_1_out), .out(Result), .sel(Opcode));  // open: in5, in6, in7

  // Notes on the sheet:
  //   Reg0
endmodule

module ContCirc8bit (
  input  C3,
  input  C2,
  input  C1,
  input  C0,
  output OP2,
  output OP1,
  output OP0,
  output RG1,
  output RG0,
  output MO1,
  output MO0,
  output ADDR3,
  output ADDR2,
  output ADDR1,
  output ADDR0
);

  wire and_1_out, and_2_out, and_3_out, and_4_out, and_5_out, and_6_out, and_10_out, and_11_out, and_12_out,
       and_13_out, and_14_out, not_1_out, not_2_out, not_3_out, not_4_out, not_5_out, not_6_out, not_7_out,
       not_8_out, not_9_out, not_10_out;

  and and_1 (and_1_out, C2, C0);
  and and_2 (and_2_out, C2, C1);
  and and_3 (and_3_out, C3, C2);
  and and_4 (and_4_out, C1, C0);
  not not_1 (not_1_out, C3);
  and and_5 (and_5_out, not_1_out, C2, not_2_out);
  not not_2 (not_2_out, C0);
  and and_6 (and_6_out, C3, C1);
  not not_3 (not_3_out, C3);
  not not_4 (not_4_out, C2);
  not not_5 (not_5_out, C0);
  and and_7 (RG1, C2, C0);
  not not_6 (not_6_out, C3);
  not not_7 (not_7_out, C2);
  not not_8 (not_8_out, C1);
  not not_9 (not_9_out, C0);
  and and_8 (MO1, C2, C0);
  and and_9 (MO0, C2, not_10_out);
  not not_10 (not_10_out, C0);
  or or_1 (OP2, and_1_out, and_2_out, and_3_out);
  or or_2 (OP1, and_4_out, and_5_out, and_6_out);
  and and_10 (and_10_out, not_3_out, not_4_out, C1, not_5_out);
  or or_3 (OP0, and_10_out, and_11_out, and_12_out);
  and and_11 (and_11_out, C2, C0);
  and and_12 (and_12_out, C3, C0);
  and and_13 (and_13_out, not_6_out, not_7_out, not_8_out, C0);
  or or_4 (RG0, and_13_out, and_14_out);
  and and_14 (and_14_out, C2, not_9_out);

  assign ADDR0 = C0;
  assign ADDR1 = C1;
  assign ADDR2 = C2;
  assign ADDR3 = 1'b0;
endmodule
